# Fritzing sketch FlyElectronicLoad (saved by Fritzing 0.9.3b)
breadboards: 1
perfboards: 1

parts:
  元件1 = Arduino Pro Mini v13
  Q1 = Basic FET N-Channel [package="D2Pak [SMD]"]
  S1 = Momentary Switch [package=ksa_sealed_tac_switch]
  J1 = Screw terminal - 2 pins [part_number=Battery package=THT]
  R1 = Resistor [tolerance=±5% resistance=220 package="2010 [SMD]"]
  R2 = Resistor [tolerance=±5% resistance=10k package="0402 [SMD]"]
  R3 = Resistor [tolerance=±5% resistance=10k package="0402 [SMD]"]
  R4 = Resistor [tolerance=±5% resistance=220 package="1206 [SMD]"]

nets:
  N1: 元件1.GND, J1.pin2, R1.Pin_1, R2.Pin_1
  N2: 元件1.VCC, S1.2
  N3: 元件1.A1, R3.Pin_0
  N4: 元件1.A0, Q1.source, R1.Pin_0
  N5: 元件1.D9_PWM, Q1.Gate
  N6: Q1.drain, J1.pin1, R3.Pin_1
  N7: S1.3, R4.Pin_1
